# Fritzing sketch breadboard (saved by Fritzing 0.9.3b)
breadboards: 3
stripboards: 6

parts:
  IC1 = IC, DIP package, 20 pins [chip_label=LS245]
  IC2 = IC, DIP package, 16 pins [chip_label=LS173]
  IC3 = IC, DIP package, 16 pins [chip_label=LS173]
  IC4 = IC, DIP package, 16 pins [chip_label=LS173]
  IC5 = IC, DIP package, 16 pins [chip_label=LS173]
  IC6 = IC, DIP package, 20 pins [chip_label=LS245]
  IC7 = IC, DIP package, 16 pins [chip_label=LS283]
  IC8 = IC, DIP package, 16 pins [chip_label=LS283]
  IC9 = IC, DIP package, 20 pins [chip_label=LS245]
  IC10 = IC, DIP package, 14 pins [chip_label=LS86]
  IC11 = IC, DIP package, 14 pins [chip_label=LS86]

nets:
  N1: IC1.pin1, IC1.pin20, IC2.pin16, IC3.pin16, IC4.pin16, IC5.pin16, IC6.pin1, IC6.pin20, IC7.pin16, IC8.pin16, IC9.pin1, IC9.pin20, IC10.pin14, IC11.pin14
  N2: IC1.pin2, IC2.pin3, IC10.pin2
  N3: IC1.pin3, IC2.pin4, IC10.pin5
  N4: IC1.pin4, IC2.pin5, IC10.pin10
  N5: IC1.pin5, IC2.pin6, IC10.pin13
  N6: IC1.pin6, IC3.pin3, IC11.pin2
  N7: IC1.pin7, IC3.pin4, IC11.pin5
  N8: IC1.pin8, IC3.pin5, IC11.pin10
  N9: IC1.pin9, IC3.pin6, IC11.pin13
  N10: IC1.pin10, IC2.pin1, IC2.pin2, IC2.pin8, IC3.pin1, IC3.pin2, IC3.pin8, IC4.pin1, IC4.pin2, IC4.pin8, IC5.pin1, IC5.pin2, IC5.pin8, IC6.pin10, IC7.pin8, IC8.pin8, IC9.pin10, IC10.pin7, IC11.pin7
  N11: IC1.pin11, IC3.pin11, IC5.pin11, IC6.pin11, IC9.pin11
  N12: IC1.pin12, IC3.pin12, IC5.pin12, IC6.pin12, IC9.pin12
  N13: IC1.pin13, IC3.pin13, IC5.pin13, IC6.pin13, IC9.pin13
  N14: IC1.pin14, IC3.pin14, IC5.pin14, IC6.pin14, IC9.pin14
  N15: IC1.pin15, IC2.pin11, IC4.pin11, IC6.pin15, IC9.pin15
  N16: IC1.pin16, IC2.pin12, IC4.pin12, IC6.pin16, IC9.pin16
  N17: IC1.pin17, IC2.pin13, IC4.pin13, IC6.pin17, IC9.pin17
  N18: IC1.pin18, IC2.pin14, IC4.pin14, IC6.pin18, IC9.pin18
  N19: IC1.pin19, IC2.pin9, IC2.pin10, IC3.pin9, IC3.pin10
  N20: IC4.pin3, IC6.pin2, IC7.pin12
  N21: IC4.pin4, IC6.pin3, IC7.pin14
  N22: IC4.pin5, IC6.pin4, IC7.pin3
  N23: IC4.pin6, IC6.pin5, IC7.pin5
  N24: IC4.pin9, IC4.pin10, IC5.pin9, IC5.pin10
  N25: IC5.pin3, IC6.pin6, IC8.pin12
  N26: IC5.pin4, IC6.pin7, IC8.pin14
  N27: IC5.pin5, IC6.pin8, IC8.pin3
  N28: IC5.pin6, IC6.pin9, IC8.pin5
  N29: IC7.pin1, IC9.pin4
  N30: IC7.pin2, IC10.pin8
  N31: IC7.pin4, IC9.pin5
  N32: IC7.pin6, IC10.pin11
  N33: IC7.pin7, IC8.pin9
  N34: IC7.pin10, IC9.pin2
  N35: IC7.pin11, IC10.pin3
  N36: IC7.pin13, IC9.pin3
  N37: IC7.pin15, IC10.pin6
  N38: IC8.pin1, IC9.pin8
  N39: IC8.pin2, IC11.pin8
  N40: IC8.pin4, IC9.pin9
  N41: IC8.pin6, IC11.pin11
  N42: IC8.pin7, IC10.pin1, IC10.pin4, IC10.pin9, IC10.pin12, IC11.pin1, IC11.pin4, IC11.pin9, IC11.pin12
  N43: IC8.pin10, IC9.pin6
  N44: IC8.pin11, IC11.pin3
  N45: IC8.pin13, IC9.pin7
  N46: IC8.pin15, IC11.pin6
