# Fritzing sketch breadboard (saved by Fritzing 0.9.3b)
breadboards: 3
stripboards: 3

parts:
  IC1 = IC, DIP package, 20 pins [chip_label=LS245]
  IC2 = IC, DIP package, 16 pins [chip_label=LS173]
  IC3 = IC, DIP package, 16 pins [chip_label=LS173]
  IC4 = IC, DIP package, 16 pins [chip_label=LS173]
  IC5 = IC, DIP package, 16 pins [chip_label=LS173]
  IC6 = IC, DIP package, 20 pins [chip_label=LS245]
  IC7 = IC, DIP package, 16 pins [chip_label=LS283]
  IC8 = IC, DIP package, 16 pins [chip_label=LS283]
  IC9 = IC, DIP package, 20 pins [chip_label=LS245]
  IC10 = IC, DIP package, 14 pins [chip_label=LS86]  # not connected
  IC11 = IC, DIP package, 14 pins [chip_label=LS86]  # not connected

nets:
  N1: IC1.pin1, IC1.pin20, IC2.pin16, IC3.pin16, IC4.pin16, IC5.pin16, IC6.pin1, IC6.pin20, IC7.pin16, IC8.pin16, IC9.pin20
  N2: IC1.pin2, IC2.pin3
  N3: IC1.pin3, IC2.pin4
  N4: IC1.pin4, IC2.pin5
  N5: IC1.pin5, IC2.pin6
  N6: IC1.pin6, IC3.pin3
  N7: IC1.pin7, IC3.pin4
  N8: IC1.pin8, IC3.pin5
  N9: IC1.pin9, IC3.pin6
  N10: IC1.pin10, IC2.pin8, IC3.pin8, IC4.pin8, IC5.pin8, IC6.pin10, IC7.pin8, IC8.pin8, IC9.pin10
  N11: IC1.pin11, IC6.pin11
  N12: IC1.pin12, IC6.pin12
  N13: IC1.pin13, IC6.pin13
  N14: IC1.pin14, IC6.pin14
  N15: IC1.pin15, IC6.pin15
  N16: IC1.pin16, IC6.pin16
  N17: IC1.pin17, IC6.pin17
  N18: IC1.pin18, IC6.pin18
  N19: IC4.pin3, IC6.pin2
  N20: IC4.pin4, IC6.pin3
  N21: IC4.pin5, IC6.pin4
  N22: IC4.pin6, IC6.pin5
  N23: IC5.pin3, IC6.pin6, IC8.pin12
  N24: IC5.pin4, IC6.pin7, IC8.pin14
  N25: IC5.pin5, IC6.pin8, IC8.pin3
  N26: IC5.pin6, IC6.pin9, IC8.pin5
  N27: IC7.pin7, IC8.pin9
